# Fritzing sketch voltage measurement (saved by Fritzing 0.9.3b)
circuit board: 8.46667cm x 5.64444cm
breadboards: 1

parts:
  R1 = Resistor [tolerance=±1% resistance=1.5k package="0402 [SMD]"]
  R2 = Resistor [tolerance=±1% resistance=47k package="0402 [SMD]"]
  ESP32_lolin32-lite = Wemos Lolin32lite
  U1 = LIPO-1000mAh [package=lipo-1000]

nets:
  N1: R1.Pin_0, U1.+
  N2: R1.Pin_1, R2.Pin_1, ESP32_lolin32-lite.pin_8
  N3: R2.Pin_0, ESP32_lolin32-lite.pin_13, U1.-

custom parts:
  Wemos Lolin32lite: Wemos Lolinlite32 wifi and blue tooth board based on the ESP-32 cpu, digital I/Os 19, analog inputs 6, clock 240mhz, Flash 4Mbytes, lipo battery charger (500ma connection broken out on breadboard but not pcb), usb.
